// Logisim project lab04.circ as structural Verilog: 9 circuits, main circuit RS-trigger asynchronous
module RS_trigger_asynchronous (
  input  R,
  input  S,
  output not_Q,
  output Q
);

  wire nand_1_out, nand_2_out;

  not nand_1 (nand_1_out, R);  // NAND_Gate
  not nand_2 (nand_2_out, S);  // NAND_Gate
  nand nand_3 (not_Q, nand_1_out, Q);
  nand nand_4 (Q, not_Q, nand_2_out);
endmodule

module RS_trigger_synchronous (
  input  S,
  input  C,
  input  R,
  output Q,
  output not_Q
);

  wire nand_1_out, nand_2_out;

  nand nand_1 (nand_1_out, S, C);
  nand nand_2 (nand_2_out, C, R);
  nand nand_3 (Q, nand_1_out, not_Q);
  nand nand_4 (not_Q, Q, nand_2_out);
endmodule

module JK_trigger (
  input  Jump,
  input  Clock,
  input  Kill,
  output Q,
  output Not_Q
);

  wire and_1_out, and_2_out, not_1_out, s_r_ff_1_q, s_r_ff_1_qn;

  and and_1 (and_1_out, Not_Q, Jump);
  and and_2 (and_2_out, Kill, Q);
  S_R_Flip_Flop #(.trigger("high")) s_r_ff_1 (
    .S(and_1_out), .clk(Clock), .R(and_2_out), .Q(s_r_ff_1_q), .Qn(s_r_ff_1_qn));  // open: preset, reset, en
  not not_1 (not_1_out, Clock);
  S_R_Flip_Flop s_r_ff_2 (
    .S(s_r_ff_1_q), .clk(not_1_out), .R(s_r_ff_1_qn), .Q(Q), .Qn(Not_Q));  // open: preset, reset, en
endmodule

module D_trigger (
  input  D,
  input  Clk,
  output Q,
  output not_Q
);

  wire not_1_out;

  not not_1 (not_1_out, D);
  S_R_Flip_Flop #(.trigger("high")) s_r_ff_1 (
    .S(D), .clk(Clk), .R(not_1_out), .Q(Q), .Qn(not_Q));  // open: preset, reset, en
endmodule

module T_trigger (
  input  Toggles,
  output Q,
  output not_Q
);

  S_R_Flip_Flop s_r_ff_1 (.S(not_Q), .clk(Toggles), .R(Q), .Q(Q), .Qn(not_Q));  // open: preset, reset, en
endmodule

module Counter (
  input  in_1,
  output [3:0] out_2
);

  wire clock_1_out, j_k_ff_1_q, j_k_ff_2_q;

  Clock clock_1 (.out(clock_1_out));
  J_K_Flip_Flop #(.trigger("falling")) j_k_ff_1 (
    .J(in_1), .clk(clock_1_out), .K(in_1), .Q(j_k_ff_1_q));  // open: Qn, preset, en, reset
  J_K_Flip_Flop #(.trigger("falling")) j_k_ff_2 (
    .J(in_1), .clk(j_k_ff_1_q), .K(in_1), .Q(j_k_ff_2_q));  // open: Qn, preset, en, reset
  and and_1 (out_2[0], ~j_k_ff_1_q, ~j_k_ff_2_q);  // AND_Gate
  and and_2 (out_2[1], j_k_ff_1_q, ~j_k_ff_2_q);  // AND_Gate
  and and_3 (out_2[2], ~j_k_ff_1_q, j_k_ff_2_q);  // AND_Gate
  and and_4 (out_2[3], j_k_ff_1_q, j_k_ff_2_q);
  // Probe on out_2
endmodule

module _8_bit_register (
  input  \Сlock ,
  input  Reset,
  input  [7:0] D,
  output [7:0] Q
);

  D_Flip_Flop d_ff_1 (.clk(\Сlock ), .D(D[0]), .Q(Q[0]), .reset(Reset));  // open: Qn, preset, en
  D_Flip_Flop d_ff_2 (.clk(\Сlock ), .D(D[1]), .Q(Q[1]), .reset(Reset));  // open: Qn, preset, en
  D_Flip_Flop d_ff_3 (.clk(\Сlock ), .D(D[2]), .Q(Q[2]), .reset(Reset));  // open: Qn, preset, en
  D_Flip_Flop d_ff_4 (.clk(\Сlock ), .D(D[3]), .Q(Q[3]), .reset(Reset));  // open: Qn, preset, en
  D_Flip_Flop d_ff_5 (.clk(\Сlock ), .D(D[4]), .Q(Q[4]), .reset(Reset));  // open: Qn, preset, en
  D_Flip_Flop d_ff_6 (.clk(\Сlock ), .D(D[5]), .Q(Q[5]), .reset(Reset));  // open: Qn, preset, en
  D_Flip_Flop d_ff_7 (.clk(\Сlock ), .D(D[6]), .Q(Q[6]), .reset(Reset));  // open: Qn, preset, en
  D_Flip_Flop d_ff_8 (.clk(\Сlock ), .D(D[7]), .Q(Q[7]), .reset(Reset));  // open: Qn, preset, en
endmodule

module Memory (
  input  [7:0] in_1,
  input  in_2,
  input  [1:0] in_3,
  output [7:0] out_4
);

  wire clock_1_out, demultiplexer_1_out0, demultiplexer_1_out1, demultiplexer_1_out2, demultiplexer_1_out3;
  wire [7:0] n8_bit_register_1_q, n8_bit_register_2_q, n8_bit_register_3_q, n8_bit_register_4_q;

  Demultiplexer #(.select(2), .enable("false")) demultiplexer_1 (
    .out0(demultiplexer_1_out0), .out1(demultiplexer_1_out1), .out2(demultiplexer_1_out2),
    .out3(demultiplexer_1_out3), .in(in_2), .sel(in_3));
  Clock clock_1 (.out(clock_1_out));
  _8_bit_register u_8_bit_register_1 (
    .\Сlock (demultiplexer_1_out0), .Reset(clock_1_out), .D(in_1), .Q(n8_bit_register_1_q));
  _8_bit_register u_8_bit_register_2 (
    .\Сlock (demultiplexer_1_out1), .Reset(clock_1_out), .D(in_1), .Q(n8_bit_register_2_q));
  _8_bit_register u_8_bit_register_3 (
    .\Сlock (demultiplexer_1_out2), .Reset(clock_1_out), .D(in_1), .Q(n8_bit_register_3_q));
  _8_bit_register u_8_bit_register_4 (
    .\Сlock (demultiplexer_1_out3), .Reset(clock_1_out), .D(in_1), .Q(n8_bit_register_4_q));
  Multiplexer #(.select(2), .width(8), .enable("false")) multiplexer_1 (
    .in0(n8_bit_register_1_q), .in1(n8_bit_register_2_q), .in2(n8_bit_register_3_q),
    .in3(n8_bit_register_4_q), .out(out_4), .sel(in_3));
endmodule

module Mod_sum (
  input  [7:0] in_1,
  input  Clock,
  input  Reset,
  input  [7:0] in_4,
  input  in_5,
  output [7:0] out_6
);

  wire [7:0] adder_1_out, multiplexer_1_out;

  // Probe on in_1
  // Probe on in_4
  // Probe on adder_1_out
  Adder adder_1 (.a(in_1), .b(multiplexer_1_out), .out(adder_1_out));  // open: cin, cout
  Multiplexer #(.width(8), .enable("false")) multiplexer_1 (
    .in0(in_4), .in1(out_6), .out(multiplexer_1_out), .sel(in_5));
  _8_bit_register u_8_bit_register_1 (.\Сlock (Clock), .Reset(Reset), .D(adder_1_out), .Q(out_6));
endmodule
